// Logisim project szamonkero2_nyitott_kollektor.circ as structural Verilog: 1 circuit, main circuit main
module main (
  input  A,
  input  E,
  input  C,
  input  B,
  output X
);

  wire not_3_out, pull_resistor_1_node, pull_resistor_3_node, pull_resistor_4_node;

  not not_1 (X, A);
  Pull_Resistor #(.pull(1)) pull_resistor_1 (.node(pull_resistor_1_node));
  not not_2 (pull_resistor_1_node, E);
  not not_3 (not_3_out, C);
  Pull_Resistor #(.pull(1)) pull_resistor_2 (.node(not_3_out));
  Pull_Resistor #(.pull(1)) pull_resistor_3 (.node(pull_resistor_3_node));
  not not_4 (pull_resistor_3_node, B);
  Pull_Resistor #(.pull(1)) pull_resistor_4 (.node(pull_resistor_4_node));
  not not_5 (pull_resistor_4_node, pull_resistor_1_node);
  not not_6 (pull_resistor_4_node, not_3_out);
  not not_7 (X, pull_resistor_3_node);
  Pull_Resistor #(.pull(1)) pull_resistor_5 (.node(X));
  not not_8 (X, pull_resistor_4_node);

  // Notes on the sheet:
  //   not_1 drives only 0 and floats otherwise
  //   not_2 drives only 0 and floats otherwise
  //   not_3 drives only 0 and floats otherwise
  //   not_4 drives only 0 and floats otherwise
  //   not_5 drives only 0 and floats otherwise
  //   not_6 drives only 0 and floats otherwise
  //   not_7 drives only 0 and floats otherwise
  //   not_8 drives only 0 and floats otherwise
endmodule
