// Logisim project szamonkero2_tri_state_KIZARO_VAGY.circ as structural Verilog: 1 circuit, main circuit main
module main (
  input  A,
  input  B,
  output Y
);

  wire not_1_out, not_2_out;

  not not_1 (not_1_out, A);
  assign Y = B ? not_1_out : 1'bz;  // Controlled_Buffer BUFFER
  not not_2 (not_2_out, B);
  assign Y = not_2_out ? A : 1'bz;  // Controlled_Buffer BUFFER_2
endmodule
