// Logisim project kimenetek_osszekozhetosege.circ as structural Verilog: 1 circuit, main circuit main
module main (
  input  A,
  input  A_2,
  input  B,
  input  A_3,
  input  A_4,
  input  B_2,
  input  A_5,
  input  A_6,
  input  B_3,
  input  A_7,
  input  A_8,
  input  EA,
  input  EA_2,
  input  B_4,
  input  EB,
  output Y,
  output Y_2,
  output Y_3,
  output Y_4,
  output Y_5,
  output Y_6,
  output Y_7,
  output Y_8
);

  wire pull_resistor_3_node, pull_resistor_4_node, pull_resistor_5_node, pull_resistor_6_node;

  not not_1 (Y, A);
  not not_2 (Y_3, A_3);
  not not_3 (Y_6, A_6);
  assign Y_7 = EA ? A_7 : 1'bz;  // Controlled_Buffer CONTROLLED_BUFFER
  Pull_Resistor #(.pull(1)) pull_resistor_1 (.node(Y_3));
  Pull_Resistor pull_resistor_2 (.node(Y_6));
  not not_4 (Y_2, A_2);
  not not_5 (Y_2, B);
  Pull_Resistor #(.pull(1)) pull_resistor_3 (.node(pull_resistor_3_node));
  not not_6 (pull_resistor_3_node, A_4);
  Pull_Resistor #(.pull(1)) pull_resistor_4 (.node(pull_resistor_4_node));
  not not_7 (pull_resistor_4_node, B_2);
  Pull_Resistor pull_resistor_5 (.node(pull_resistor_5_node));
  not not_8 (pull_resistor_5_node, A_5);
  Pull_Resistor pull_resistor_6 (.node(pull_resistor_6_node));
  not not_9 (pull_resistor_6_node, B_3);
  assign Y_8 = EA_2 ? A_8 : 1'bz;  // Controlled_Buffer CONTROLLED_BUFFER_2
  assign Y_8 = EB ? B_4 : 1'bz;  // Controlled_Buffer CONTROLLED_BUFFER_3
  Pull_Resistor #(.pull(1)) pull_resistor_7 (.node(Y_4));
  not not_10 (Y_4, pull_resistor_3_node);
  not not_11 (Y_4, pull_resistor_4_node);
  Pull_Resistor pull_resistor_8 (.node(Y_5));
  not not_12 (Y_5, pull_resistor_5_node);
  not not_13 (Y_5, pull_resistor_6_node);

  // Notes on the sheet:
  //   1.TOTEM-POLE KIEMENET
  //   2. NYITOTT-KOLLEKTOROS KIMENET
  //   not_2 drives only 0 and floats otherwise
  //   3. NYITOTT-EMITTERES KIMENET
  //   not_3 drives only 1 and floats otherwise
  //   4.TRI-STATE KIMENET
  //   Tilos összekötni bármilyen kimenettel!
  //   not_6 drives only 0 and floats otherwise
  //   not_7 drives only 0 and floats otherwise
  //   Az össze kapcsolt nyitott kollektoros kimenetek 
  //   logikai ÉS kapcsolatot valósítanak meg!
  //   not_8 drives only 1 and floats otherwise
  //   not_9 drives only 1 and floats otherwise
  //   Az össze kapcsolt nyitott emitteres kimenetek 
  //   logikai VAGY kapcsolatot valósítanak meg!
  //   A kimenetek összeköthetőek , de kizárólag 1 buffer lehet aktív.
  //   KIZÁRÓ-VAGY jelleggel működtethetőek
  //   not_10 drives only 0 and floats otherwise
  //   not_11 drives only 0 and floats otherwise
  //   not_12 drives only 1 and floats otherwise
  //   not_13 drives only 1 and floats otherwise
endmodule
