// Logisim project onellenorzo_nyitott_kollektoros.circ as structural Verilog: 1 circuit, main circuit main
module main (
  input  E,
  input  D,
  input  C,
  input  B,
  input  A,
  output Y
);

  wire not_1_out, not_2_out, not_3_out, not_4_out, not_6_out;

  not not_1 (not_1_out, C);
  not not_2 (not_2_out, B);
  not not_3 (not_3_out, A);
  not not_4 (not_4_out, E);
  not not_5 (not_4_out, D);
  Pull_Resistor #(.pull(1)) pull_resistor_1 (.node(not_1_out));
  not not_6 (not_6_out, not_1_out);
  Pull_Resistor #(.pull(1)) pull_resistor_2 (.node(not_2_out));
  not not_7 (not_6_out, not_2_out);
  Pull_Resistor #(.pull(1)) pull_resistor_3 (.node(not_3_out));
  not not_8 (not_6_out, not_3_out);
  Pull_Resistor #(.pull(1)) pull_resistor_4 (.node(not_4_out));
  Pull_Resistor #(.pull(1)) pull_resistor_5 (.node(not_6_out));
  not not_9 (not_4_out, not_6_out);
  Pull_Resistor #(.pull(1)) pull_resistor_6 (.node(Y));
  not not_10 (Y, not_4_out);

  // Notes on the sheet:
  //   not_1 drives only 0 and floats otherwise
  //   not_2 drives only 0 and floats otherwise
  //   not_3 drives only 0 and floats otherwise
  //   not_4 drives only 0 and floats otherwise
  //   not_5 drives only 0 and floats otherwise
  //   not_6 drives only 0 and floats otherwise
  //   not_7 drives only 0 and floats otherwise
  //   not_8 drives only 0 and floats otherwise
  //   not_9 drives only 0 and floats otherwise
  //   not_10 drives only 0 and floats otherwise
endmodule
