// Logisim project onellenorzo_tri_state_eklivalencia.circ as structural Verilog: 1 circuit, main circuit main
module main (
  input  A,
  input  B,
  output Y
);

  wire not_1_out, not_2_out;

  assign Y = not_2_out ? not_1_out : 1'bz;  // Controlled_Buffer BUFFER
  not not_1 (not_1_out, A);
  not not_2 (not_2_out, B);
  assign Y = B ? A : 1'bz;  // Controlled_Buffer BUFFER_2
endmodule
