// Logisim project multiplexer_1feladat_szamonkero.circ as structural Verilog: 1 circuit, main circuit main
module main (
  input  A,
  input  B,
  input  I0,
  input  C,
  input  I2,
  input  I4,
  input  I6,
  input  I7,
  input  I1,
  input  I3,
  input  I5,
  input  E,
  output Y
);

  wire nand_1_out, nand_2_out, nand_3_out, nand_4_out, nand_5_out, nand_6_out, nand_7_out, nand_8_out,
       not_1_out, not_2_out, not_3_out;

  nand nand_1 (nand_1_out, ~A, ~B, ~C, E);  // NAND_Gate
  nand nand_2 (nand_2_out, ~A, B, ~C, E);  // NAND_Gate
  nand nand_3 (nand_3_out, ~A, ~B, C, E);  // NAND_Gate
  nand nand_4 (nand_4_out, ~A, B, C, E);  // NAND_Gate
  nand nand_5 (nand_5_out, A, B, C, E);
  nand nand_6 (nand_6_out, A, ~B, ~C, E);  // NAND_Gate
  nand nand_7 (nand_7_out, A, B, ~C, E);  // NAND_Gate
  nand nand_8 (nand_8_out, A, ~B, C, E);  // NAND_Gate
  not not_1 (not_1_out, nand_6_out);
  not not_2 (not_2_out, nand_7_out);
  not not_3 (not_3_out, nand_8_out);
  \L_eng_Y_negált  \l_eng_y_negált_1  (.I(I0), .E(nand_1_out), .out_3(Y));
  \L_eng_Y_negált  \l_eng_y_negált_2  (.I(I2), .E(nand_2_out), .out_3(Y));
  \L_eng_Y_negált  \l_eng_y_negált_3  (.I(I4), .E(nand_3_out), .out_3(Y));
  \L_eng_Y_negált  \l_eng_y_negált_4  (.I(I6), .E(nand_4_out), .out_3(Y));
  \L_eng_Y_negált  \l_eng_y_negált_5  (.I(I7), .E(nand_5_out), .out_3(Y));
  nand nand_9 (Y, I1, not_1_out);
  nand nand_10 (Y, I3, not_2_out);
  nand nand_11 (Y, I5, not_3_out);
  Pull_Resistor #(.pull(1)) pull_resistor_1 (.node(Y));

  // Notes on the sheet:
  //   nand_9 drives only 0 and floats otherwise
  //   nand_10 drives only 0 and floats otherwise
  //   nand_11 drives only 0 and floats otherwise
endmodule
