// Logisim project multiplexer_2feladat_szamonkero.circ as structural Verilog: 1 circuit, main circuit main
module main (
  input  I2,
  input  I3,
  input  I4,
  input  A,
  input  I7,
  input  B,
  input  C,
  input  I0,
  input  I1,
  input  I5,
  input  I6,
  input  nE,
  output Y
);

  wire nor_1_out, nor_2_out, nor_3_out, nor_4_out, nor_5_out, nor_6_out, nor_7_out, nor_8_out, nor_9_out,
       not_1_out;

  nor nor_1 (nor_1_out, ~B, C);  // NOR_Gate
  nor nor_2 (nor_2_out, ~A, ~B);  // NOR_Gate
  nor nor_3 (nor_3_out, A, B, ~C);  // NOR_Gate
  nor nor_4 (nor_4_out, A, B, C, nE);
  nor nor_5 (nor_5_out, ~A, B, C, nE);  // NOR_Gate
  nor nor_6 (nor_6_out, ~A, B, ~C, nE);  // NOR_Gate
  nor nor_7 (nor_7_out, A, ~B, ~C, nE);  // NOR_Gate
  not not_1 (not_1_out, nor_8_out);
  nor nor_8 (nor_8_out, nor_9_out, nE);
  nor nor_9 (nor_9_out, nor_1_out, nor_2_out, nor_3_out);
  \H_eng_Y_ponált  \h_eng_y_ponált_1  (.I(I5), .E(nor_6_out), .out_3(Y));
  \H_eng_Y_ponált  \h_eng_y_ponált_2  (.I(I6), .E(nor_7_out), .out_3(Y));
  Pull_Resistor #(.pull(1)) pull_resistor_1 (.node(Y));
  _4_1_MUX_nE_Y_Tristate u_4_1_mux_ne_y_tristate_1 (
    .I00(I2), .I01(I3), .I02(I4), .I03(I7), .A(A), .B(C), .E(not_1_out), .Y(Y));
  nand nand_1 (Y, I0, nor_4_out);
  nand nand_2 (Y, I1, nor_5_out);

  // Notes on the sheet:
  //   nand_1 drives only 0 and floats otherwise
  //   nand_2 drives only 0 and floats otherwise
endmodule
