// Logisim project multiplexer_onellenorzo.circ as structural Verilog: 1 circuit, main circuit main
module main (
  input  A,
  input  I0,
  input  B,
  input  C,
  input  I1,
  input  I2,
  input  I3,
  input  I4,
  input  I5,
  input  I6,
  input  E,
  output Y
);

  wire nand_1_out, nand_2_out, nand_3_out, nand_4_out, nand_5_out, nand_6_out, nand_7_out, not_1_out,
       not_2_out, not_3_out, not_4_out, not_5_out, not_6_out, not_7_out;

  nand nand_1 (nand_1_out, ~A, ~B, ~C, E);  // NAND_Gate
  nand nand_2 (nand_2_out, A, ~B, ~C, E);  // NAND_Gate
  nand nand_3 (nand_3_out, ~A, B, ~C, E);  // NAND_Gate
  nand nand_4 (nand_4_out, A, B, ~C, E);  // NAND_Gate
  nand nand_5 (nand_5_out, ~A, ~B, C, E);  // NAND_Gate
  nand nand_6 (nand_6_out, A, ~B, C, E);  // NAND_Gate
  nand nand_7 (nand_7_out, ~A, B, C, E);  // NAND_Gate
  not not_1 (not_1_out, nand_1_out);
  not not_2 (not_2_out, nand_2_out);
  not not_3 (not_3_out, nand_3_out);
  not not_4 (not_4_out, nand_4_out);
  not not_5 (not_5_out, nand_5_out);
  not not_6 (not_6_out, nand_6_out);
  not not_7 (not_7_out, nand_7_out);
  Pull_Resistor #(.pull(1)) pull_resistor_1 (.node(Y));
  \H_eng_Y_negált  \h_eng_y_negált_1  (.I(I0), .E(not_1_out), .out_3(Y));
  \H_eng_Y_negált  \h_eng_y_negált_2  (.I(I1), .E(not_2_out), .out_3(Y));
  \H_eng_Y_negált  \h_eng_y_negált_3  (.I(I2), .E(not_3_out), .out_3(Y));
  nand nand_8 (Y, I3, not_4_out);
  nand nand_9 (Y, I4, not_5_out);
  nand nand_10 (Y, I5, not_6_out);
  nand nand_11 (Y, I6, not_7_out);

  // Notes on the sheet:
  //   nand_8 drives only 0 and floats otherwise
  //   nand_9 drives only 0 and floats otherwise
  //   nand_10 drives only 0 and floats otherwise
  //   nand_11 drives only 0 and floats otherwise
endmodule
