// Logisim project multiplexer_onellenorzo2.circ as structural Verilog: 1 circuit, main circuit main
module main (
  input  I0,
  input  I1,
  input  I6,
  input  I7,
  input  A,
  input  B,
  input  C,
  input  I2,
  input  I3,
  input  I4,
  input  I5,
  input  E,
  output Y,
  output out_14,
  output out_15
);

  wire not_1_out, not_2_out, not_3_out, not_4_out, not_5_out, not_6_out, or_1_out, or_2_out, or_3_out,
       or_4_out, or_5_out, or_6_out, or_7_out, or_8_out;

  or or_1 (or_1_out, B, C);
  or or_2 (or_2_out, ~B, ~C);  // OR_Gate
  or or_3 (or_3_out, A, ~B, C, ~E);  // OR_Gate
  or or_4 (or_4_out, ~A, ~B, C, ~E);  // OR_Gate
  or or_5 (or_5_out, A, B, ~C, ~E);  // OR_Gate
  or or_6 (or_6_out, ~A, B, ~C, ~E);  // OR_Gate
  not not_1 (not_1_out, or_1_out);
  not not_2 (not_2_out, or_2_out);
  or or_7 (or_7_out, not_1_out, not_2_out);
  not not_3 (not_3_out, or_7_out);
  not not_4 (not_4_out, E);
  not not_5 (not_5_out, or_3_out);
  not not_6 (not_6_out, or_4_out);
  \L_eng_Y_ponált  \l_eng_y_ponált_1  (.I(I4), .E(or_5_out), .out_3(out_14));
  \L_eng_Y_ponált  \l_eng_y_ponált_2  (.I(I5), .E(or_6_out), .out_3(out_14));
  _4_1_MUX_nE_Y_Tristate u_4_1_mux_ne_y_tristate_1 (
    .I00(I0), .I01(I1), .I02(I6), .I03(I7), .A(A), .B(B), .E(or_8_out), .Y(out_14));
  or or_8 (or_8_out, not_3_out, not_4_out);
  nand nand_1 (out_14, I2, not_5_out);
  nand nand_2 (out_14, I3, not_6_out);
  Pull_Resistor #(.pull(1)) pull_resistor_1 (.node(out_14));

  assign out_15 = out_14;
  assign Y = out_14;

  // Notes on the sheet:
  //   nand_1 drives only 0 and floats otherwise
  //   nand_2 drives only 0 and floats otherwise
endmodule
