// Logisim project hazardmentesites_onellenorzo.circ as structural Verilog: 1 circuit, main circuit main
module main (
  input  A,
  input  B,
  input  D,
  input  C,
  output Y
);

  wire nand_1_out, nand_2_out, nand_3_out;

  nand nand_1 (nand_1_out, ~A, B, D);  // NAND_Gate
  nand nand_2 (nand_2_out, A, C, D);
  nand nand_3 (nand_3_out, B, C, D);
  nand nand_4 (Y, nand_1_out, nand_2_out, nand_3_out);
endmodule
