// Logisim project 7.feladat NAND.circ as structural Verilog: 1 circuit, main circuit main
module main (
  input  A,
  input  B,
  input  C,
  input  D,
  input  E,
  output Y
);

  wire nand_1_out, nand_2_out, nand_3_out, nand_4_out, nand_5_out, nand_6_out;

  nand nand_1 (nand_1_out, B, B);
  nand nand_2 (nand_2_out, C, D);
  nand nand_3 (nand_3_out, D, D);
  nand nand_4 (nand_4_out, E, E);
  nand nand_5 (nand_5_out, nand_1_out, nand_2_out);
  nand nand_6 (nand_6_out, A, nand_5_out, nand_3_out, nand_4_out);
  nand nand_7 (Y, nand_6_out, nand_6_out);
endmodule
