// Logisim project 8.feladat NAND.circ as structural Verilog: 1 circuit, main circuit main
module main (
  input  E,
  input  D,
  input  C,
  input  A,
  output out_5
);

  wire nand_1_out, nand_2_out, nand_3_out, nand_4_out;

  nand nand_1 (nand_1_out, E, E);
  nand nand_2 (nand_2_out, D, D);
  nand nand_3 (nand_3_out, C, A);
  nand nand_4 (nand_4_out, nand_1_out, nand_2_out, nand_3_out);
  nand nand_5 (out_5, nand_4_out, nand_4_out);
endmodule
