// Logisim project 8.feladat NOR.circ as structural Verilog: 1 circuit, main circuit main
module main (
  input  E,
  input  D,
  input  C,
  input  A,
  output out_5
);

  wire nor_1_out, nor_2_out, nor_3_out;

  nor nor_1 (nor_1_out, C, C);
  nor nor_2 (nor_2_out, A, A);
  nor nor_3 (nor_3_out, nor_1_out, nor_2_out);
  nor nor_4 (out_5, E, D, nor_3_out);
endmodule
