// Logisim project 9.feladat NAND.circ as structural Verilog: 1 circuit, main circuit main
module main (
  input  E,
  input  D,
  input  C,
  input  A,
  output out_5
);

  wire nand_1_out, nand_2_out, nand_3_out;

  nand nand_1 (nand_1_out, C, C);
  nand nand_2 (nand_2_out, A, A);
  nand nand_3 (nand_3_out, nand_1_out, nand_2_out);
  nand nand_4 (out_5, E, D, nand_3_out);
endmodule
