// Logisim project 9.feladat NOR.circ as structural Verilog: 1 circuit, main circuit main
module main (
  input  E,
  input  D,
  input  C,
  input  A,
  output out_5
);

  wire nor_1_out, nor_2_out, nor_3_out, nor_4_out;

  nor nor_1 (nor_1_out, E, E);
  nor nor_2 (nor_2_out, D, D);
  nor nor_3 (nor_3_out, C, A);
  nor nor_4 (nor_4_out, nor_1_out, nor_2_out, nor_3_out);
  nor nor_5 (out_5, nor_4_out, nor_4_out);
endmodule
