// Logisim project 2.feladat_NOR_NAND.circ as structural Verilog: 1 circuit, main circuit main
module main (
  input  A,
  input  B,
  input  C,
  input  D,
  input  E,
  input  A_2,
  input  B_2,
  input  C_2,
  input  D_2,
  input  E_2,
  output out_11,
  output out_12
);

  wire nand_1_out, nand_2_out, nand_3_out, nand_4_out, nand_5_out, nor_1_out, nor_2_out, nor_3_out, nor_4_out;

  nor nor_1 (nor_1_out, ~D, E);  // NOR_Gate
  nor nor_2 (nor_2_out, ~A, ~C, ~D);  // NOR_Gate
  nor nor_3 (nor_3_out, A, ~B, E);  // NOR_Gate
  nor nor_4 (nor_4_out, A, ~B, D);  // NOR_Gate
  nand nand_1 (nand_1_out, D_2, ~E_2);  // NAND_Gate
  nand nand_2 (nand_2_out, A_2, C_2, D_2);
  nand nand_3 (nand_3_out, ~A_2, B_2, ~E_2);  // NAND_Gate
  nand nand_4 (nand_4_out, ~A_2, B_2, ~D_2);  // NAND_Gate
  nor nor_5 (out_11, nor_1_out, nor_2_out, nor_3_out, nor_4_out);
  nand nand_5 (nand_5_out, nand_1_out, nand_2_out, nand_3_out, nand_4_out);
  nand nand_6 (out_12, nand_5_out, nand_5_out);
endmodule
