// Logisim project 6.feladat_nyitott_kollektor.circ as structural Verilog: 1 circuit, main circuit main
module main (
  input  A,
  input  B,
  input  C,
  input  D,
  input  E,
  output Y
);

  wire not_9_out, pull_resistor_1_node, pull_resistor_2_node, pull_resistor_3_node, pull_resistor_4_node,
       pull_resistor_5_node;

  Pull_Resistor #(.pull(1)) pull_resistor_1 (.node(pull_resistor_1_node));
  not not_1 (pull_resistor_1_node, A);
  Pull_Resistor #(.pull(1)) pull_resistor_2 (.node(pull_resistor_2_node));
  not not_2 (pull_resistor_2_node, B);
  Pull_Resistor #(.pull(1)) pull_resistor_3 (.node(pull_resistor_3_node));
  not not_3 (pull_resistor_3_node, C);
  Pull_Resistor #(.pull(1)) pull_resistor_4 (.node(pull_resistor_4_node));
  not not_4 (pull_resistor_4_node, D);
  not not_5 (pull_resistor_4_node, E);
  Pull_Resistor #(.pull(1)) pull_resistor_5 (.node(pull_resistor_5_node));
  not not_6 (pull_resistor_5_node, pull_resistor_1_node);
  not not_7 (pull_resistor_5_node, pull_resistor_2_node);
  not not_8 (pull_resistor_5_node, pull_resistor_3_node);
  not not_9 (not_9_out, pull_resistor_4_node);
  Pull_Resistor #(.pull(1)) pull_resistor_6 (.node(not_9_out));
  not not_10 (not_9_out, pull_resistor_5_node);
  Pull_Resistor #(.pull(1)) pull_resistor_7 (.node(Y));
  not not_11 (Y, not_9_out);

  // Notes on the sheet:
  //   not_1 drives only 0 and floats otherwise
  //   not_2 drives only 0 and floats otherwise
  //   not_3 drives only 0 and floats otherwise
  //   not_4 drives only 0 and floats otherwise
  //   not_5 drives only 0 and floats otherwise
  //   not_6 drives only 0 and floats otherwise
  //   not_7 drives only 0 and floats otherwise
  //   not_8 drives only 0 and floats otherwise
  //   not_9 drives only 0 and floats otherwise
  //   not_10 drives only 0 and floats otherwise
  //   not_11 drives only 0 and floats otherwise
endmodule
