// Logisim project 7.feladat_tri_state_EKLIVALENCIA.circ as structural Verilog: 1 circuit, main circuit main
module main (
  input  A,
  input  B,
  output out_3
);

  wire not_1_out, not_2_out, not_3_out, not_4_out;

  assign out_3 = not_1_out ? A : 1'bz;  // Controlled_Buffer BUFFER
  not not_1 (not_1_out, not_2_out);
  not not_2 (not_2_out, B);
  not not_3 (not_3_out, B);
  assign out_3 = not_3_out ? not_4_out : 1'bz;  // Controlled_Buffer BUFFER_2
  not not_4 (not_4_out, A);
endmodule
