// Logisim project 8.feladat_multiplexer.circ as structural Verilog: 1 circuit, main circuit main
module main (
  input  A,
  input  B,
  input  I0,
  input  C,
  input  I4,
  input  I6,
  input  I5,
  input  I1,
  input  I2,
  input  I3,
  input  I7,
  input  E,
  output out_13
);

  wire and_1_out, and_2_out, and_3_out, and_4_out, and_5_out, and_6_out, and_7_out, and_8_out, not_1_out,
       not_2_out, not_3_out;

  and and_1 (and_1_out, A, ~B, C, E);  // AND_Gate
  and and_2 (and_2_out, ~A, B, C, E);  // AND_Gate
  and and_3 (and_3_out, A, ~B, ~C, E);  // AND_Gate
  and and_4 (and_4_out, ~A, B, ~C, E);  // AND_Gate
  and and_5 (and_5_out, A, B, ~C, E);  // AND_Gate
  and and_6 (and_6_out, A, B, C, E);
  not not_1 (not_1_out, and_1_out);
  not not_2 (not_2_out, and_2_out);
  and and_7 (and_7_out, ~A, ~B, E);  // AND_Gate
  and and_8 (and_8_out, not_1_out, not_2_out);
  _2_1_MUX_nE u_2_1_mux_ne_1 (.I0(I0), .I1(I4), .S(C), .nE(not_3_out), .Y(out_13));
  not not_3 (not_3_out, and_7_out);
  _2_1_MUX_nE u_2_1_mux_ne_2 (.I0(I6), .I1(I5), .S(A), .nE(and_8_out), .Y(out_13));
  nand nand_1 (out_13, I1, and_3_out);
  nand nand_2 (out_13, I2, and_4_out);
  nand nand_3 (out_13, I3, and_5_out);
  nand nand_4 (out_13, I7, and_6_out);
  Pull_Resistor #(.pull(1)) pull_resistor_1 (.node(out_13));

  // Notes on the sheet:
  //   nand_1 drives only 0 and floats otherwise
  //   nand_2 drives only 0 and floats otherwise
  //   nand_3 drives only 0 and floats otherwise
  //   nand_4 drives only 0 and floats otherwise
endmodule
