// Logisim project 6.feladat_leptetoReg_allapotBejaras.circ as structural Verilog: 1 circuit, main circuit main
module main (
  input  NRES
);

  wire and_1_out, and_2_out, and_3_out, CLK_out, hc195_shift_reg_async_clear_1_nqd,
       hc195_shift_reg_async_clear_1_qa, hc195_shift_reg_async_clear_1_qb, hc195_shift_reg_async_clear_1_qc,
       hc195_shift_reg_async_clear_1_qd, nand_1_out, nand_2_out, not_1_out, or_1_out;

  and and_1 (and_1_out, nand_1_out, nand_2_out);
  nand nand_1 (nand_1_out, hc195_shift_reg_async_clear_1_nqd, hc195_shift_reg_async_clear_1_qc, ~hc195_shift_reg_async_clear_1_qb, hc195_shift_reg_async_clear_1_qa);  // NAND_Gate
  nand nand_2 (nand_2_out, hc195_shift_reg_async_clear_1_qd, ~hc195_shift_reg_async_clear_1_qc, ~hc195_shift_reg_async_clear_1_qb, ~hc195_shift_reg_async_clear_1_qa);  // NAND_Gate
  not not_1 (not_1_out, nand_1_out);
  LED QD (.in(hc195_shift_reg_async_clear_1_qd));
  LED QB (.in(hc195_shift_reg_async_clear_1_qb));
  LED QC (.in(hc195_shift_reg_async_clear_1_qc));
  LED QA (.in(hc195_shift_reg_async_clear_1_qa));
  HC195_Shift_Reg_Async_Clear hc195_shift_reg_async_clear_1 (
    .nCLR(NRES), .SH_LD(and_1_out), .CLK(CLK_out), .SI(or_1_out), .A(nand_1_out), .B(not_1_out),
    .C(not_1_out), .D(nand_1_out), .QA(hc195_shift_reg_async_clear_1_qa),
    .QB(hc195_shift_reg_async_clear_1_qb), .QC(hc195_shift_reg_async_clear_1_qc),
    .QD(hc195_shift_reg_async_clear_1_qd), .nQD(hc195_shift_reg_async_clear_1_nqd));
  and and_2 (and_2_out, hc195_shift_reg_async_clear_1_qd, hc195_shift_reg_async_clear_1_qb, ~hc195_shift_reg_async_clear_1_qa);  // AND_Gate
  and and_3 (and_3_out, hc195_shift_reg_async_clear_1_nqd, hc195_shift_reg_async_clear_1_qa);
  Clock CLK (.out(CLK_out));
  or or_1 (or_1_out, and_2_out, and_3_out, ~hc195_shift_reg_async_clear_1_qc);  // OR_Gate
endmodule
