// Logisim project 7.feladat_leptetoReg.circ as structural Verilog: 1 circuit, main circuit main
module main (
  input  RES,
  output out_2
);

  wire A_out, and_1_out, and_2_out, and_3_out, and_4_out, B_out, C_out, CLK_out, D_out,
       hc195_shift_reg_async_clear_1_nqd, hc195_shift_reg_async_clear_1_qa, hc195_shift_reg_async_clear_1_qb,
       hc195_shift_reg_async_clear_1_qc, hc195_shift_reg_async_clear_1_qd, nor_1_out, nor_2_out, nor_3_out,
       nor_4_out, nor_5_out, pull_resistor_1_node;

  nor A (A_out, RES, nor_2_out);
  nor B (B_out, nor_3_out, RES, nor_5_out);
  nor C (C_out, RES, nor_3_out, nor_4_out);
  nor D (D_out, RES, nor_2_out, nor_5_out);
  LED NDEK5 (.in(nor_2_out));
  LED NDEK8 (.in(nor_3_out));
  LED NDEK10 (.in(nor_4_out));
  LED NDEK11 (.in(nor_5_out));
  nor nor_1 (nor_1_out, RES, nor_2_out, nor_3_out, nor_4_out, nor_5_out);
  nor nor_2 (nor_2_out, hc195_shift_reg_async_clear_1_qd, ~hc195_shift_reg_async_clear_1_qc, hc195_shift_reg_async_clear_1_qb, ~hc195_shift_reg_async_clear_1_qa);  // NOR_Gate
  nor nor_3 (nor_3_out, hc195_shift_reg_async_clear_1_nqd, hc195_shift_reg_async_clear_1_qc, hc195_shift_reg_async_clear_1_qb, hc195_shift_reg_async_clear_1_qa);
  nor nor_4 (nor_4_out, hc195_shift_reg_async_clear_1_nqd, hc195_shift_reg_async_clear_1_qc, ~hc195_shift_reg_async_clear_1_qb, hc195_shift_reg_async_clear_1_qa);  // NOR_Gate
  nor nor_5 (nor_5_out, hc195_shift_reg_async_clear_1_nqd, hc195_shift_reg_async_clear_1_qc, ~hc195_shift_reg_async_clear_1_qb, ~hc195_shift_reg_async_clear_1_qa);  // NOR_Gate
  Pull_Resistor #(.pull(1)) pull_resistor_1 (.node(pull_resistor_1_node));
  LED QD (.in(hc195_shift_reg_async_clear_1_qd));
  LED QC (.in(hc195_shift_reg_async_clear_1_qc));
  LED C_2 (.in(C_out));
  LED D_2 (.in(D_out));
  LED QB (.in(hc195_shift_reg_async_clear_1_qb));
  LED QA (.in(hc195_shift_reg_async_clear_1_qa));
  LED A_2 (.in(A_out));
  LED B_2 (.in(B_out));
  and and_1 (and_1_out, hc195_shift_reg_async_clear_1_qd, ~hc195_shift_reg_async_clear_1_qc);  // AND_Gate
  and and_2 (and_2_out, hc195_shift_reg_async_clear_1_qd, hc195_shift_reg_async_clear_1_qb);
  and and_3 (and_3_out, hc195_shift_reg_async_clear_1_qa, hc195_shift_reg_async_clear_1_qb, ~hc195_shift_reg_async_clear_1_qc);  // AND_Gate
  and and_4 (and_4_out, ~hc195_shift_reg_async_clear_1_qc, ~hc195_shift_reg_async_clear_1_qb, ~hc195_shift_reg_async_clear_1_qa);  // AND_Gate
  LED SI (.in(out_2));
  HC195_Shift_Reg_Async_Clear hc195_shift_reg_async_clear_1 (
    .nCLR(pull_resistor_1_node), .SH_LD(nor_1_out), .CLK(CLK_out), .SI(out_2), .A(A_out), .B(B_out),
    .C(C_out), .D(D_out), .QA(hc195_shift_reg_async_clear_1_qa), .QB(hc195_shift_reg_async_clear_1_qb),
    .QC(hc195_shift_reg_async_clear_1_qc), .QD(hc195_shift_reg_async_clear_1_qd),
    .nQD(hc195_shift_reg_async_clear_1_nqd));
  LED SH_nLD (.in(nor_1_out));
  or or_1 (out_2, and_4_out, and_3_out, and_2_out, and_1_out);
  Clock CLK (.out(CLK_out));
endmodule
