// Logisim project 6.feladat_163.circ as structural Verilog: 1 circuit, main circuit main
module main (
  input  ENT,
  input  ENP,
  input  NRES
);

  wire and_1_out, and_2_out, CLK_out, n163_hex_sync_clear_1_qa, n163_hex_sync_clear_1_qb,
       n163_hex_sync_clear_1_qc, n163_hex_sync_clear_1_qd, n163_hex_sync_clear_1_tc, not_1_out, not_2_out,
       or_1_out, or_2_out, or_3_out, or_4_out, pull_resistor_1_node;

  and and_1 (and_1_out, or_1_out, NRES);
  or or_1 (or_1_out, ~n163_hex_sync_clear_1_qd, ~n163_hex_sync_clear_1_qc, ~n163_hex_sync_clear_1_qb, n163_hex_sync_clear_1_qa);  // OR_Gate
  Pull_Resistor #(.pull(1)) pull_resistor_1 (.node(pull_resistor_1_node));
  LED QD (.in(n163_hex_sync_clear_1_qd));
  LED QC (.in(n163_hex_sync_clear_1_qc));
  LED QA (.in(n163_hex_sync_clear_1_qa));
  LED QB (.in(n163_hex_sync_clear_1_qb));
  _163_Hex_Sync_Clear u_163_hex_sync_clear_1 (
    .nCLEAR(and_1_out), .nLOAD(and_2_out), .D(pull_resistor_1_node), .C(or_2_out), .B(not_2_out),
    .A(not_1_out), .ET(ENT), .EP(ENP), .CLK(CLK_out), .TC(n163_hex_sync_clear_1_tc),
    .QD(n163_hex_sync_clear_1_qd), .QC(n163_hex_sync_clear_1_qc), .QB(n163_hex_sync_clear_1_qb),
    .QA(n163_hex_sync_clear_1_qa));
  Clock CLK (.out(CLK_out));
  and and_2 (and_2_out, or_4_out, or_3_out, or_2_out);
  not not_1 (not_1_out, or_2_out);
  not not_2 (not_2_out, or_4_out);
  or or_2 (or_2_out, n163_hex_sync_clear_1_qd, ~n163_hex_sync_clear_1_qc, ~n163_hex_sync_clear_1_qb, ~n163_hex_sync_clear_1_qa);  // OR_Gate
  or or_3 (or_3_out, ~n163_hex_sync_clear_1_qd, n163_hex_sync_clear_1_qc, ~n163_hex_sync_clear_1_qb, n163_hex_sync_clear_1_qa);  // OR_Gate
  or or_4 (or_4_out, ~n163_hex_sync_clear_1_qd, ~n163_hex_sync_clear_1_qc, n163_hex_sync_clear_1_qb, n163_hex_sync_clear_1_qa);  // OR_Gate
  LED QD_2 (.in(n163_hex_sync_clear_1_tc));
endmodule
