// Logisim project 7.feladat_160.circ as structural Verilog: 1 circuit, main circuit main
module main (
  input  ENT,
  input  ENP,
  input  NRES
);

  wire and_1_out, CLK_out, n160_dec_count_async_clear_1_qa, n160_dec_count_async_clear_1_qb,
       n160_dec_count_async_clear_1_qc, n160_dec_count_async_clear_1_qd, n160_dec_count_async_clear_1_tc,
       not_1_out, or_1_out, or_2_out, pull_resistor_1_node;

  LED QD (.in(n160_dec_count_async_clear_1_qd));
  not not_1 (not_1_out, n160_dec_count_async_clear_1_tc);
  LED QC (.in(n160_dec_count_async_clear_1_qc));
  LED QB (.in(n160_dec_count_async_clear_1_qb));
  LED QA (.in(n160_dec_count_async_clear_1_qa));
  Pull_Resistor #(.pull(1)) pull_resistor_1 (.node(pull_resistor_1_node));
  or or_1 (or_1_out, n160_dec_count_async_clear_1_qd, ~n160_dec_count_async_clear_1_qc, n160_dec_count_async_clear_1_qb, ~n160_dec_count_async_clear_1_qa);  // OR_Gate
  or or_2 (or_2_out, n160_dec_count_async_clear_1_qd, n160_dec_count_async_clear_1_qc, ~n160_dec_count_async_clear_1_qb, ~n160_dec_count_async_clear_1_qa);  // OR_Gate
  LED TC (.in(n160_dec_count_async_clear_1_tc));
  _160_Dec_Count_Async_Clear u_160_dec_count_async_clear_1 (
    .nCLEAR(NRES), .nLOAD(and_1_out), .D(1'b0), .C(not_1_out), .B(or_2_out), .A(pull_resistor_1_node),
    .ET(ENT), .EP(ENP), .CLK(CLK_out), .TC(n160_dec_count_async_clear_1_tc),
    .QC(n160_dec_count_async_clear_1_qc), .QB(n160_dec_count_async_clear_1_qb),
    .QA(n160_dec_count_async_clear_1_qa), .QD(n160_dec_count_async_clear_1_qd));
  Clock CLK (.out(CLK_out));
  and and_1 (and_1_out, ~n160_dec_count_async_clear_1_tc, or_2_out, or_1_out);  // AND_Gate

  // Notes on the sheet:
  //   Decimális, aszinkron törlésű számláló
  //   Megadott állapotokat bejáró szinkron sorrendi hálózat időbeli működésének vizsgálata
  //   Bejárt állapotok: NRES =>0, 1, 2, 3, 5, 7, 8, 9 és újra 3
endmodule
