// Logisim project Jnk to D flip flop.circ as structural Verilog: 1 circuit, main circuit main
module main (
  input  D,
  output Qn
);

  wire CLK_out, pull_resistor_1_node;

  \JK_negált_flip_flop  \jk_negált_flip_flop_1  (
    .J(D), .CLK(CLK_out), .K(D), .nPR(pull_resistor_1_node), .Q(Qn));  // open: nCL, nQ
  Clock CLK (.out(CLK_out));
  Pull_Resistor #(.pull(1)) pull_resistor_1 (.node(pull_resistor_1_node));
endmodule
