// Logisim project T to JnK flip flop.circ as structural Verilog: 1 circuit, main circuit main
module main (
  input  J,
  input  nK,
  output Qn
);

  wire and_1_out, and_2_out, CLK_out, or_1_out, pull_resistor_1_node, t_flip_flop_1_nq;

  and and_1 (and_1_out, t_flip_flop_1_nq, J);
  Pull_Resistor #(.pull(1)) pull_resistor_1 (.node(pull_resistor_1_node));
  T_flip_flop t_flip_flop_1 (
    .CLK(CLK_out), .T(or_1_out), .nPR(pull_resistor_1_node), .nCL(pull_resistor_1_node), .Q(Qn),
    .nQ(t_flip_flop_1_nq));
  or or_1 (or_1_out, and_1_out, and_2_out);
  Clock CLK (.out(CLK_out));
  and and_2 (and_2_out, Qn, ~nK);  // AND_Gate
endmodule
