// Logisim project szinkron_sorrendi_minta1.circ as structural Verilog: 1 circuit, main circuit main
module main (
  input  RESET,
  input  X,
  output Z1,
  output Z2,
  output Q1,
  output Q2
);

  wire and_1_out, CLK_out, not_1_out, or_2_out, or_3_out, pull_resistor_1_node, t_flip_flop_1_nq,
       t_flip_flop_2_nq;

  or or_1 (Z1, Q1, t_flip_flop_2_nq);
  T_flip_flop t_flip_flop_1 (
    .CLK(CLK_out), .T(or_2_out), .nPR(pull_resistor_1_node), .nCL(not_1_out), .Q(Q1), .nQ(t_flip_flop_1_nq));
  or or_2 (or_2_out, Q1, and_1_out);
  and and_1 (and_1_out, Q2, X);
  and and_2 (Z2, t_flip_flop_1_nq, Q2);
  T_flip_flop t_flip_flop_2 (
    .CLK(CLK_out), .T(or_3_out), .nPR(pull_resistor_1_node), .nCL(not_1_out), .Q(Q2), .nQ(t_flip_flop_2_nq));
  or or_3 (or_3_out, Q1, ~X);  // OR_Gate
  Pull_Resistor #(.pull(1)) pull_resistor_1 (.node(pull_resistor_1_node));
  not not_1 (not_1_out, RESET);
  Clock CLK (.out(CLK_out));
endmodule
