// Logisim project szinkron_sorrendi_szamonkero.circ as structural Verilog: 1 circuit, main circuit main
module main (
  input  RESET,
  input  X2,
  input  X1,
  output Q1,
  output Q2
);

  wire and_1_out, and_2_out, and_3_out, CLK_out, not_1_out, or_1_out, or_2_out, pull_resistor_1_node;

  T_flip_flop t_flip_flop_1 (
    .CLK(CLK_out), .T(or_1_out), .nPR(pull_resistor_1_node), .nCL(not_1_out), .Q(Q1));  // open: nQ
  or or_1 (or_1_out, and_1_out, and_2_out);
  and and_1 (and_1_out, Q1, X2);
  and and_2 (and_2_out, X2, X1);
  LED Z (.in(Q2));
  or or_2 (or_2_out, ~X2, X1);  // OR_Gate
  Pull_Resistor #(.pull(1)) pull_resistor_1 (.node(pull_resistor_1_node));
  JK_flip_flop jk_flip_flop_1 (
    .J(or_2_out), .CLK(CLK_out), .K(and_3_out), .nPR(pull_resistor_1_node), .nCL(not_1_out), .Q(Q2));  // open: nQ
  not not_1 (not_1_out, RESET);
  and and_3 (and_3_out, X2, Q1);
  Clock CLK (.out(CLK_out));
endmodule
