// Logisim project sorrendi_aszinkron_onellenorzo1.circ as structural Verilog: 1 circuit, main circuit main
module main (
  input  Reset,
  input  x1,
  input  x2,
  output out_4,
  output out_5
);

  wire and_2_out, and_3_out, or_1_out;

  and and_1 (out_4, ~x1, out_5);  // AND_Gate
  RS_flip_flop rs_flip_flop_1 (.S(and_2_out), .R(or_1_out), .Q(out_5));  // open: nQ
  or or_1 (or_1_out, Reset, ~x2);  // OR_Gate
  and and_2 (and_2_out, ~Reset, and_3_out);  // AND_Gate
  and and_3 (and_3_out, ~x1, x2);  // AND_Gate
endmodule
