// Logisim project sorrendi_aszinkron_szamonkero.circ as structural Verilog: 1 circuit, main circuit main
module main (
  input  Reset,
  input  X1,
  input  X2,
  output Z,
  output Q2,
  output Q1
);

  wire and_1_out, and_2_out, and_3_out, and_4_out, and_5_out, and_6_out, and_7_out, and_8_out, or_1_out,
       or_3_out, rs_flip_flop_1_nq;

  and and_1 (and_1_out, ~X2, ~X1, Q1);  // AND_Gate
  and and_2 (and_2_out, X1, ~X2, rs_flip_flop_1_nq);  // AND_Gate
  RS_flip_flop rs_flip_flop_1 (.S(and_3_out), .R(or_1_out), .nQ(rs_flip_flop_1_nq), .Q(Q1));
  or or_1 (or_1_out, Reset, ~X2);  // OR_Gate
  or or_2 (Z, and_1_out, and_2_out, and_4_out, and_7_out);
  and and_3 (and_3_out, ~Reset, ~X1, X2);  // AND_Gate
  and and_4 (and_4_out, rs_flip_flop_1_nq, Q2);
  RS_flip_flop rs_flip_flop_2 (.S(and_8_out), .R(or_3_out), .Q(Q2));  // open: nQ
  or or_3 (or_3_out, and_6_out, Reset, and_5_out);
  and and_5 (and_5_out, rs_flip_flop_1_nq, ~X2);  // AND_Gate
  and and_6 (and_6_out, ~X1, ~X2);  // AND_Gate
  and and_7 (and_7_out, Q2, ~X1);  // AND_Gate
  and and_8 (and_8_out, ~Reset, X2);  // AND_Gate
endmodule
