// Logisim project 3bit_sorrendi_szamonkero.circ as structural Verilog: 1 circuit, main circuit main
module main (
  input  R,
  input  E,
  output QC,
  output QB,
  output QA
);

  wire and_1_out, and_2_out, and_3_out, and_4_out, and_5_out, and_6_out, and_7_out, and_8_out, and_9_out,
       CLK_out, or_1_out, or_2_out, or_3_out, pull_resistor_1_node;

  Pull_Resistor #(.pull(1)) pull_resistor_1 (.node(pull_resistor_1_node));
  Clock CLK (.out(CLK_out));
  and and_1 (and_1_out, R, ~QC);  // AND_Gate
  LED led_1 (.in(QC));
  T_flip_flop t_flip_flop_1 (
    .CLK(CLK_out), .T(or_1_out), .nPR(pull_resistor_1_node), .nCL(pull_resistor_1_node), .Q(QC));  // open: nQ
  or or_1 (or_1_out, and_1_out, and_2_out, and_3_out);
  and and_2 (and_2_out, E, ~QC, QB);  // AND_Gate
  and and_3 (and_3_out, E, ~R, QB, QA);  // AND_Gate
  and and_4 (and_4_out, E, ~R, QA);  // AND_Gate
  LED led_2 (.in(QB));
  JK_flip_flop jk_flip_flop_1 (
    .J(and_4_out), .CLK(CLK_out), .K(or_2_out), .nPR(pull_resistor_1_node), .nCL(pull_resistor_1_node), .Q(QB));  // open: nQ
  or or_2 (or_2_out, R, and_5_out);
  and and_5 (and_5_out, E, QA);
  and and_6 (and_6_out, ~E, QA);  // AND_Gate
  LED led_3 (.in(QA));
  or or_3 (or_3_out, and_6_out, and_7_out, R, and_8_out, and_9_out);
  and and_7 (and_7_out, E, QB, ~QA);  // AND_Gate
  D_flip_flop d_flip_flop_1 (
    .CLK(CLK_out), .D(or_3_out), .nPR(pull_resistor_1_node), .nCL(pull_resistor_1_node), .Q(QA));  // open: nQ
  and and_8 (and_8_out, E, ~QC, ~QB);  // AND_Gate
  and and_9 (and_9_out, E, ~QB, ~QA);  // AND_Gate

  // Notes on the sheet:
  //   RES=>5,6,7,0,1,3,4,5 és újra 6-ról
endmodule
