// Logisim project szinkSorr_leptetoReg_onellenorzo.circ as structural Verilog: 1 circuit, main circuit main
module main (
  input  NRES
);

  wire and_1_out, and_2_out, and_3_out, CLK_out, NDEK2_out, NDEK8_out, NDEK9_out, not_1_out, or_1_out,
       pull_resistor_1_node, shift_reg_sync_clear_1_qa, shift_reg_sync_clear_1_qb, shift_reg_sync_clear_1_qc,
       shift_reg_sync_clear_1_qd;

  LED QC (.in(shift_reg_sync_clear_1_qc));
  LED QD (.in(shift_reg_sync_clear_1_qd));
  not not_1 (not_1_out, NDEK9_out);
  LED QA (.in(shift_reg_sync_clear_1_qa));
  LED QB (.in(shift_reg_sync_clear_1_qb));
  Shift_Reg_Sync_Clear shift_reg_sync_clear_1 (
    .nCLR(NRES), .SH_LD(and_3_out), .CLK(CLK_out), .SI(or_1_out), .A(pull_resistor_1_node), .B(NDEK8_out),
    .C(not_1_out), .D(NDEK2_out), .QA(shift_reg_sync_clear_1_qa), .QB(shift_reg_sync_clear_1_qb),
    .QC(shift_reg_sync_clear_1_qc), .QD(shift_reg_sync_clear_1_qd));  // open: nQD
  Pull_Resistor #(.pull(1)) pull_resistor_1 (.node(pull_resistor_1_node));
  nand NDEK2 (NDEK2_out, ~shift_reg_sync_clear_1_qd, ~shift_reg_sync_clear_1_qc, shift_reg_sync_clear_1_qb, ~shift_reg_sync_clear_1_qa);  // NAND_Gate
  nand NDEK8 (NDEK8_out, shift_reg_sync_clear_1_qd, ~shift_reg_sync_clear_1_qc, ~shift_reg_sync_clear_1_qb, ~shift_reg_sync_clear_1_qa);  // NAND_Gate
  nand NDEK9 (NDEK9_out, shift_reg_sync_clear_1_qd, ~shift_reg_sync_clear_1_qc, ~shift_reg_sync_clear_1_qb, shift_reg_sync_clear_1_qa);  // NAND_Gate
  and and_1 (and_1_out, ~shift_reg_sync_clear_1_qa, ~shift_reg_sync_clear_1_qd);  // AND_Gate
  and and_2 (and_2_out, shift_reg_sync_clear_1_qb, ~shift_reg_sync_clear_1_qc);  // AND_Gate
  Clock CLK (.out(CLK_out));
  and and_3 (and_3_out, NDEK9_out, NDEK8_out, NDEK2_out);
  or or_1 (or_1_out, and_1_out, and_2_out);

  // Notes on the sheet:
  //   Bejárandó állapotok: 
  //   Megadott állapotokat bejáró szinkron sorrendi hálózat tervezése léptetőregiszterrel
  //   NRES => 0,1,2,3,7,14,12,8,9,15 és újra 14
endmodule
