// Logisim project szinkSorr_leptetoReg_szamonkero.circ as structural Verilog: 1 circuit, main circuit main
module main (
  input  NRES
);

  wire and_1_out, and_2_out, and_3_out, and_4_out, CLK_out, NDEK5_out, NDEK9_out, or_1_out, or_2_out,
       pull_resistor_1_node, pull_resistor_2_node, shift_reg_sync_clear_1_qa, shift_reg_sync_clear_1_qb,
       shift_reg_sync_clear_1_qc, shift_reg_sync_clear_1_qd;

  LED QD (.in(shift_reg_sync_clear_1_qd));
  Pull_Resistor #(.pull(1)) pull_resistor_1 (.node(pull_resistor_1_node));
  and and_1 (and_1_out, NRES, NDEK5_out);
  LED QB (.in(shift_reg_sync_clear_1_qb));
  LED QC (.in(shift_reg_sync_clear_1_qc));
  Pull_Resistor #(.pull(1)) pull_resistor_2 (.node(pull_resistor_2_node));
  LED QA (.in(shift_reg_sync_clear_1_qa));
  nand NDEK5 (NDEK5_out, ~shift_reg_sync_clear_1_qd, shift_reg_sync_clear_1_qc, ~shift_reg_sync_clear_1_qb, shift_reg_sync_clear_1_qa);  // NAND_Gate
  nand NDEK9 (NDEK9_out, shift_reg_sync_clear_1_qd, ~shift_reg_sync_clear_1_qc, ~shift_reg_sync_clear_1_qb, shift_reg_sync_clear_1_qa);  // NAND_Gate
  and and_2 (and_2_out, ~shift_reg_sync_clear_1_qa, shift_reg_sync_clear_1_qd);  // AND_Gate
  and and_3 (and_3_out, shift_reg_sync_clear_1_qa, ~shift_reg_sync_clear_1_qd);  // AND_Gate
  Shift_Reg_Sync_Clear shift_reg_sync_clear_1 (
    .nCLR(pull_resistor_1_node), .SH_LD(and_4_out), .CLK(CLK_out), .SI(or_2_out), .A(or_1_out),
    .B(pull_resistor_2_node), .C(or_1_out), .D(and_1_out), .QA(shift_reg_sync_clear_1_qa),
    .QB(shift_reg_sync_clear_1_qb), .QC(shift_reg_sync_clear_1_qc), .QD(shift_reg_sync_clear_1_qd));  // open: nQD
  or or_1 (or_1_out, ~NRES, ~NDEK5_out);  // OR_Gate
  or or_2 (or_2_out, and_2_out, ~shift_reg_sync_clear_1_qb, and_3_out);  // OR_Gate
  Clock CLK (.out(CLK_out));
  and and_4 (and_4_out, NDEK9_out, NDEK5_out, NRES);

  // Notes on the sheet:
  //   Bejárandó állapotok: 
  //   Megadott állapotokat bejáró szinkron sorrendi hálózat tervezése léptetőregiszterrel
  //   NRES => 7,15,14,13,11,6,12,9,10,5 és újra 7
endmodule
