// Logisim project szamlalo_szamonkero.circ as structural Verilog: 1 circuit, main circuit main
module main (
  input  NRES
);

  wire and_1_out, and_2_out, clock_1_out, n161_hex_count_async_clear_1_qa, n161_hex_count_async_clear_1_qb,
       n161_hex_count_async_clear_1_qc, n161_hex_count_async_clear_1_qd, n161_hex_count_async_clear_1_tc,
       NDEK2_out, NDEK12_out, not_1_out, pull_resistor_1_node;

  Pull_Resistor #(.pull(1)) pull_resistor_1 (.node(pull_resistor_1_node));
  LED QC (.in(n161_hex_count_async_clear_1_qc));
  LED QD (.in(n161_hex_count_async_clear_1_qd));
  and and_1 (and_1_out, NRES, NDEK2_out);
  LED QA (.in(n161_hex_count_async_clear_1_qa));
  LED QB (.in(n161_hex_count_async_clear_1_qb));
  _161_Hex_Count_Async_Clear u_161_hex_count_async_clear_1 (
    .nCLEAR(pull_resistor_1_node), .nLOAD(and_2_out), .D(and_1_out), .C(NRES), .B(and_1_out), .A(not_1_out),
    .ET(pull_resistor_1_node), .EP(pull_resistor_1_node), .CLK(clock_1_out),
    .TC(n161_hex_count_async_clear_1_tc), .QD(n161_hex_count_async_clear_1_qd),
    .QC(n161_hex_count_async_clear_1_qc), .QB(n161_hex_count_async_clear_1_qb),
    .QA(n161_hex_count_async_clear_1_qa));
  and and_2 (and_2_out, NDEK12_out, NDEK2_out, NRES);
  not not_1 (not_1_out, NRES);
  nand NDEK2 (NDEK2_out, ~n161_hex_count_async_clear_1_qd, ~n161_hex_count_async_clear_1_qc, n161_hex_count_async_clear_1_qb, ~n161_hex_count_async_clear_1_qa);  // NAND_Gate
  nand NDEK12 (NDEK12_out, n161_hex_count_async_clear_1_qd, n161_hex_count_async_clear_1_qc, ~n161_hex_count_async_clear_1_qb, ~n161_hex_count_async_clear_1_qa);  // NAND_Gate
  LED TC (.in(n161_hex_count_async_clear_1_tc));
  Clock clock_1 (.out(clock_1_out));

  // Notes on the sheet:
  //   Megadott állapotokat bejáró szinkron sorrendi hálózat tervezése aszinkron törlésű hexadecimális számlálóval
  //   Bejárandó állapotok: NRES => 1, 2, 4, 5, 6, 7, 8, 9, 10, 11, 12, 14, 15, 0 és újra 1
endmodule
