// Logisim project 10_feladat_leptetoReg.circ as structural Verilog: 1 circuit, main circuit main
module main (
  input  NRES
);

  wire and_1_out, and_2_out, and_3_out, and_4_out, CLK_out, nand_1_out, nand_2_out, nand_3_out, NDEK2_out,
       NDEK8_out, NDEK9_out, NDEK15_out, or_1_out, pull_resistor_1_node, shift_reg_sync_clear_1_qa,
       shift_reg_sync_clear_1_qb, shift_reg_sync_clear_1_qc, shift_reg_sync_clear_1_qd;

  LED QD (.in(shift_reg_sync_clear_1_qd));
  Pull_Resistor #(.pull(1)) pull_resistor_1 (.node(pull_resistor_1_node));
  nand nand_1 (nand_1_out, NRES, NDEK8_out, NDEK9_out);
  LED QB (.in(shift_reg_sync_clear_1_qb));
  LED QC (.in(shift_reg_sync_clear_1_qc));
  nand nand_2 (nand_2_out, NRES, NDEK2_out, NDEK9_out);
  nand nand_3 (nand_3_out, NRES, NDEK9_out);
  LED QA (.in(shift_reg_sync_clear_1_qa));
  Shift_Reg_Sync_Clear shift_reg_sync_clear_1 (
    .nCLR(pull_resistor_1_node), .SH_LD(and_4_out), .CLK(CLK_out), .SI(or_1_out), .A(and_1_out),
    .B(nand_2_out), .C(nand_3_out), .D(nand_1_out), .QA(shift_reg_sync_clear_1_qa),
    .QB(shift_reg_sync_clear_1_qb), .QC(shift_reg_sync_clear_1_qc), .QD(shift_reg_sync_clear_1_qd));  // open: nQD
  and and_1 (and_1_out, NRES, NDEK15_out);
  nand NDEK2 (NDEK2_out, ~shift_reg_sync_clear_1_qd, ~shift_reg_sync_clear_1_qc, shift_reg_sync_clear_1_qb, ~shift_reg_sync_clear_1_qa);  // NAND_Gate
  nand NDEK8 (NDEK8_out, shift_reg_sync_clear_1_qd, ~shift_reg_sync_clear_1_qc, ~shift_reg_sync_clear_1_qb, ~shift_reg_sync_clear_1_qa);  // NAND_Gate
  nand NDEK9 (NDEK9_out, shift_reg_sync_clear_1_qd, ~shift_reg_sync_clear_1_qc, ~shift_reg_sync_clear_1_qb, shift_reg_sync_clear_1_qa);  // NAND_Gate
  nand NDEK15 (NDEK15_out, shift_reg_sync_clear_1_qd, shift_reg_sync_clear_1_qc, shift_reg_sync_clear_1_qb, shift_reg_sync_clear_1_qa);
  and and_2 (and_2_out, ~shift_reg_sync_clear_1_qa, ~shift_reg_sync_clear_1_qd);  // AND_Gate
  or or_1 (or_1_out, and_2_out, and_3_out);
  and and_3 (and_3_out, shift_reg_sync_clear_1_qb, ~shift_reg_sync_clear_1_qc);  // AND_Gate
  Clock CLK (.out(CLK_out));
  and and_4 (and_4_out, NRES, NDEK15_out, NDEK9_out, NDEK8_out, NDEK2_out);

  // Notes on the sheet:
  //   Bejárandó állapotok: 
  //   Megadott állapotokat bejáró szinkron sorrendi hálózat tervezése léptetőregiszterrel
  //   NRES => 14, 12, 8, 9, 15, 0, 1, 2, 3, 7, 14
endmodule
