// Logisim project 4.feladat_JK_T.circ as structural Verilog: 1 circuit, main circuit main
module main (
  input  T,
  output Qn
);

  wire CLK_out, pull_resistor_1_node;

  JK_flip_flop jk_flip_flop_1 (
    .J(T), .CLK(CLK_out), .K(T), .nPR(pull_resistor_1_node), .nCL(pull_resistor_1_node), .Q(Qn));  // open: nQ
  Clock CLK (.out(CLK_out));
  Pull_Resistor #(.pull(1)) pull_resistor_1 (.node(pull_resistor_1_node));
endmodule
