// Logisim project 7.feladat_aszinkron_.circ as structural Verilog: 1 circuit, main circuit main
module main (
  input  X1,
  input  X2,
  input  RES,
  output Q1,
  output Q2
);

  wire and_1_out, and_2_out, and_3_out, and_4_out, or_1_out, or_2_out;

  or or_1 (or_1_out, and_1_out, RES);
  and and_1 (and_1_out, ~X1, X2);  // AND_Gate
  RS_flip_flop rs_flip_flop_1 (.S(and_2_out), .R(or_1_out), .Q(Q1));  // open: nQ
  and and_2 (and_2_out, X1, ~RES, Q2);  // AND_Gate
  LED Z (.in(and_3_out));
  and and_3 (and_3_out, ~Q1, Q2);  // AND_Gate
  RS_flip_flop rs_flip_flop_2 (.S(and_4_out), .R(or_1_out), .Q(Q2));  // open: nQ
  and and_4 (and_4_out, ~RES, or_2_out);  // AND_Gate
  or or_2 (or_2_out, ~X2, X1);  // OR_Gate
endmodule
