// Logisim project 8_feladat_3bit_szinkron.circ as structural Verilog: 1 circuit, main circuit main
module main (
  input  RES,
  input  E
);

  wire and_1_out, and_2_out, and_3_out, and_4_out, and_5_out, and_6_out, CLK_out, d_flip_flop_1_q,
       jk_flip_flop_1_q, not_1_out, or_1_out, or_2_out, pull_resistor_1_node, t_flip_flop_1_q;

  and and_1 (and_1_out, d_flip_flop_1_q, ~E);  // AND_Gate
  LED QC (.in(d_flip_flop_1_q));
  D_flip_flop d_flip_flop_1 (
    .CLK(CLK_out), .D(or_1_out), .nPR(pull_resistor_1_node), .nCL(not_1_out), .Q(d_flip_flop_1_q));  // open: nQ
  or or_1 (or_1_out, and_1_out, and_2_out, and_3_out);
  and and_2 (and_2_out, d_flip_flop_1_q, ~t_flip_flop_1_q);  // AND_Gate
  and and_3 (and_3_out, E, ~jk_flip_flop_1_q);  // AND_Gate
  LED QB (.in(t_flip_flop_1_q));
  T_flip_flop t_flip_flop_1 (
    .CLK(CLK_out), .T(or_2_out), .nPR(not_1_out), .nCL(pull_resistor_1_node), .Q(t_flip_flop_1_q));  // open: nQ
  or or_2 (or_2_out, and_4_out, and_5_out);
  and and_4 (and_4_out, jk_flip_flop_1_q, E);
  and and_5 (and_5_out, ~d_flip_flop_1_q, t_flip_flop_1_q, E);  // AND_Gate
  LED QA (.in(jk_flip_flop_1_q));
  JK_flip_flop jk_flip_flop_1 (
    .J(and_6_out), .CLK(CLK_out), .K(E), .nPR(pull_resistor_1_node), .nCL(not_1_out), .Q(jk_flip_flop_1_q));  // open: nQ
  and and_6 (and_6_out, d_flip_flop_1_q, E);
  not not_1 (not_1_out, RES);
  Pull_Resistor #(.pull(1)) pull_resistor_1 (.node(pull_resistor_1_node));
  Clock CLK (.out(CLK_out));

  // Notes on the sheet:
  //   RES=>2,4,5,6,7,0 és újra 4
endmodule
