// Logisim project 11.feladat_szinkron_flipflop_sorrendi_idobeli.circ as structural Verilog: 1 circuit, main circuit main
module main (
  input  RES,
  input  E
);

  wire and_1_out, and_2_out, and_3_out, and_4_out, and_5_out, and_6_out, and_7_out, and_8_out, CLK_out,
       d_flip_flop_1_nq, d_flip_flop_1_q, jk_flip_flop_1_nq, jk_flip_flop_1_q, not_1_out, or_1_out, or_2_out,
       pull_resistor_1_node, t_flip_flop_1_nq, t_flip_flop_1_q;

  and and_1 (and_1_out, ~E, d_flip_flop_1_q);  // AND_Gate
  LED QC (.in(d_flip_flop_1_q));
  D_flip_flop d_flip_flop_1 (
    .CLK(CLK_out), .D(or_1_out), .nPR(pull_resistor_1_node), .nCL(not_1_out), .Q(d_flip_flop_1_q),
    .nQ(d_flip_flop_1_nq));
  or or_1 (or_1_out, and_1_out, and_3_out, and_2_out, and_4_out);
  and and_2 (and_2_out, E, t_flip_flop_1_q, jk_flip_flop_1_nq);
  and and_3 (and_3_out, d_flip_flop_1_q, t_flip_flop_1_nq, jk_flip_flop_1_q);
  and and_4 (and_4_out, E, d_flip_flop_1_nq, jk_flip_flop_1_nq);
  and and_5 (and_5_out, E, jk_flip_flop_1_q);
  LED QB (.in(t_flip_flop_1_q));
  T_flip_flop t_flip_flop_1 (
    .CLK(CLK_out), .T(or_2_out), .nPR(pull_resistor_1_node), .nCL(not_1_out), .Q(t_flip_flop_1_q),
    .nQ(t_flip_flop_1_nq));
  or or_2 (or_2_out, and_5_out, and_7_out, and_6_out);
  and and_6 (and_6_out, E, d_flip_flop_1_nq, t_flip_flop_1_q);
  and and_7 (and_7_out, E, d_flip_flop_1_q, t_flip_flop_1_nq);
  LED QA (.in(jk_flip_flop_1_q));
  and and_8 (and_8_out, E, t_flip_flop_1_q);
  Pull_Resistor #(.pull(1)) pull_resistor_1 (.node(pull_resistor_1_node));
  JK_flip_flop jk_flip_flop_1 (
    .J(and_8_out), .CLK(CLK_out), .K(E), .nPR(not_1_out), .nCL(pull_resistor_1_node), .Q(jk_flip_flop_1_q),
    .nQ(jk_flip_flop_1_nq));
  not not_1 (not_1_out, RES);
  Clock CLK (.out(CLK_out));
endmodule
