// Logisim project 5.feladat_4bites_szinkron_szamlalo.circ as structural Verilog: 1 circuit, main circuit main
module main (
  input  RES
);

  wire CLK_out, DEK7_out, DEK10_out, DEK12_out, DEK14_out, n163_hex_sync_clear_1_qa,
       n163_hex_sync_clear_1_qb, n163_hex_sync_clear_1_qc, n163_hex_sync_clear_1_qd,
       n163_hex_sync_clear_1_tc, nor_1_out, not_1_out, not_2_out, or_1_out, pull_resistor_1_node;

  Pull_Resistor #(.pull(1)) pull_resistor_1 (.node(pull_resistor_1_node));
  not not_1 (not_1_out, RES);
  not not_2 (not_2_out, DEK14_out);
  LED QD (.in(n163_hex_sync_clear_1_qd));
  LED QB (.in(n163_hex_sync_clear_1_qb));
  LED QC (.in(n163_hex_sync_clear_1_qc));
  or or_1 (or_1_out, DEK12_out, DEK10_out);
  LED QA (.in(n163_hex_sync_clear_1_qa));
  LED TC (.in(n163_hex_sync_clear_1_tc));
  _163_Hex_Sync_Clear u_163_hex_sync_clear_1 (
    .nCLEAR(not_1_out), .nLOAD(nor_1_out), .D(not_2_out), .C(or_1_out), .B(DEK12_out), .A(DEK7_out),
    .ET(pull_resistor_1_node), .EP(pull_resistor_1_node), .CLK(CLK_out), .TC(n163_hex_sync_clear_1_tc),
    .QD(n163_hex_sync_clear_1_qd), .QC(n163_hex_sync_clear_1_qc), .QB(n163_hex_sync_clear_1_qb),
    .QA(n163_hex_sync_clear_1_qa));
  Clock CLK (.out(CLK_out));
  nor nor_1 (nor_1_out, DEK14_out, DEK12_out, DEK10_out, DEK7_out);
  and DEK7 (DEK7_out, ~n163_hex_sync_clear_1_qd, n163_hex_sync_clear_1_qc, n163_hex_sync_clear_1_qb, n163_hex_sync_clear_1_qa);  // AND_Gate
  and DEK10 (DEK10_out, n163_hex_sync_clear_1_qd, ~n163_hex_sync_clear_1_qc, n163_hex_sync_clear_1_qb, ~n163_hex_sync_clear_1_qa);  // AND_Gate
  and DEK12 (DEK12_out, n163_hex_sync_clear_1_qd, n163_hex_sync_clear_1_qc, ~n163_hex_sync_clear_1_qb, ~n163_hex_sync_clear_1_qa);  // AND_Gate
  and DEK14 (DEK14_out, n163_hex_sync_clear_1_qd, n163_hex_sync_clear_1_qc, n163_hex_sync_clear_1_qb, ~n163_hex_sync_clear_1_qa);  // AND_Gate

  // Notes on the sheet:
  //   4bites szinkron számláló tervezése szinkron törlésű szinkron számlálóval
  //   RES => 0, 1, 2, 3, 4, 5, 6, 7, 9, 10, 12, 14 és újra 0
endmodule
