// Logisim project Count Clear Load lib.circ as structural Verilog
module Sinc_Clear_Load (
  input  nCLEAR,
  input  nLOAD,
  input  Dbe,
  input  X,
  output Dki
);

  wire and_1_out, and_2_out;

  and and_1 (and_1_out, nCLEAR, nLOAD, Dbe);
  and and_2 (and_2_out, nCLEAR, ~nLOAD, X);  // AND_Gate
  or or_1 (Dki, and_1_out, and_2_out);
endmodule

module ASinc_Pre (
  input  nCLR,
  input  nLOAD,
  input  X,
  output PRE
);

  and and_1 (PRE, nCLR, nLOAD, X);
endmodule

module ASinc_Clr (
  input  nCLAR,
  input  nLOAD,
  input  X,
  output CLR
);

  wire and_1_out, and_2_out;

  and and_1 (and_1_out, nCLAR, nLOAD);
  and and_2 (and_2_out, nCLAR, X);
  nor nor_1 (CLR, and_1_out, and_2_out);
endmodule

module Sinc_Load (
  input  nLOAD,
  input  Dbe,
  input  X,
  output Dki
);

  wire and_1_out, and_2_out;

  and and_1 (and_1_out, nLOAD, Dbe);
  and and_2 (and_2_out, ~nLOAD, X);  // AND_Gate
  or or_1 (Dki, and_1_out, and_2_out);
endmodule
