// Logisim project MUX lib.circ as structural Verilog
module _4_1_MUX_nE_Y_Tristate (
  input  I00,
  input  I01,
  input  I02,
  input  I03,
  input  A,
  input  B,
  input  E,
  output Y
);

  wire not_1_out;

  not not_1 (not_1_out, E);
  Multiplexer #(.select(2)) multiplexer_1 (
    .in0(I00), .in1(I01), .in2(I02), .in3(I03), .out(Y), .sel({B, A}), .en(not_1_out));
endmodule

module _4_1_MUX_E_Y_Tristate (
  input  I00,
  input  I01,
  input  I02,
  input  I03,
  input  A,
  input  B,
  input  E,
  output Y
);

  Multiplexer #(.select(2)) multiplexer_1 (.in0(I00), .in1(I01), .in2(I02), .in3(I03), .out(Y), .sel({B, A}), .en(E));
endmodule

module _2_1_MUX_nE (
  input  I0,
  input  I1,
  input  S,
  input  nE,
  output Y
);

  wire not_1_out;

  Multiplexer multiplexer_1 (.in0(I0), .in1(I1), .out(Y), .sel(S), .en(not_1_out));
  not not_1 (not_1_out, nE);
endmodule

module _2__1_MUX_E (
  input  I0,
  input  I1,
  input  S,
  input  E,
  output Y
);

  Multiplexer multiplexer_1 (.in0(I0), .in1(I1), .out(Y), .sel(S), .en(E));
endmodule
