// Logisim project TriState lib.circ as structural Verilog
module \H_eng_Y_ponált  (
  input  I,
  input  E,
  output out_3
);

  assign out_3 = E ? I : 1'bz;  // Controlled_Buffer controlled_buffer_1
endmodule

module \H_eng_Y_negált  (
  input  I,
  input  E,
  output out_3
);

  assign out_3 = E ? ~I : 1'bz;  // Controlled_Inverter controlled_inverter_1
endmodule

module \L_eng_Y_ponált  (
  input  I,
  input  E,
  output out_3
);

  wire not_1_out;

  assign out_3 = not_1_out ? I : 1'bz;  // Controlled_Buffer controlled_buffer_1
  not not_1 (not_1_out, E);
endmodule

module \L_eng_Y_negált  (
  input  I,
  input  E,
  output out_3
);

  wire not_1_out;

  assign out_3 = not_1_out ? ~I : 1'bz;  // Controlled_Inverter controlled_inverter_1
  not not_1 (not_1_out, E);
endmodule
