// Logisim project counters lib.circ as structural Verilog: 5 circuits, main circuit main
module main (
);

  _160_Dec_Count_Async_Clear u_160_dec_count_async_clear_1 ();  // open: nCLEAR, nLOAD, D, C, B, A, ET, EP, CLK, TC, QC, QB, QA, QD
  _162_Dec_Count_Sync_Clear u_162_dec_count_sync_clear_1 ();  // open: nCLEAR, nLOAD, D, C, B, A, ET, EP, CLK, TC, QC, QB, QA, QD
  _161_Hex_Count_Async_Clear u_161_hex_count_async_clear_1 ();  // open: nCLEAR, nLOAD, D, C, B, A, ET, EP, CLK, TC, QD, QC, QB, QA
  _163_Hex_Sync_Clear u_163_hex_sync_clear_1 ();  // open: nCLEAR, nLOAD, D, C, B, A, ET, EP, CLK, TC, QD, QC, QB, QA

  // Notes on the sheet:
  //   160 Decimális számláló aszinkron törléssel és szinkron betöltéssel
  //   162 Decimális számláló szinkron törléssel és szinkron betöltéssel
  //   161 Hexadecimális számláló aszinkron törléssel és szinkron betöltéssel
  //   163 Hexadecimális számláló szinkron törléssel és szinkron betöltéssel
endmodule

module _162_Dec_Count_Sync_Clear (
  input  nCLEAR,
  input  nLOAD,
  input  D,
  input  C,
  input  B,
  input  A,
  input  ET,
  input  EP,
  input  CLK,
  output TC,
  output QC,
  output QB,
  output QA,
  output QD
);

  wire and_1_out, and_2_out, and_3_out, and_4_out, and_5_out, and_6_out, and_7_out, and_8_out, and_9_out,
       and_10_out, and_11_out, d_ff_1_qn, d_ff_2_qn, d_ff_3_qn, d_ff_4_qn, or_1_out, or_2_out, or_3_out,
       or_4_out, or_5_out, sinc_clear_load_1_dki, sinc_clear_load_2_dki, sinc_clear_load_3_dki,
       sinc_clear_load_4_dki;

  or or_1 (or_1_out, and_1_out, and_2_out);
  and and_1 (and_1_out, QA, QB, QC);
  and and_2 (and_2_out, d_ff_4_qn, d_ff_2_qn, QD);
  or or_2 (or_2_out, and_4_out, and_5_out, and_6_out);
  and and_3 (and_3_out, ET, EP);
  and and_4 (and_4_out, d_ff_3_qn, QC);
  and and_5 (and_5_out, d_ff_2_qn, QA, QB);
  and and_6 (and_6_out, QB, d_ff_4_qn, QC);
  Sinc_Clear_Load sinc_clear_load_1 (
    .nCLEAR(nCLEAR), .nLOAD(nLOAD), .Dbe(or_1_out), .X(D), .Dki(sinc_clear_load_1_dki));
  or or_3 (or_3_out, ~nLOAD, and_3_out);  // OR_Gate
  or or_4 (or_4_out, and_7_out, and_8_out);
  Sinc_Clear_Load sinc_clear_load_2 (
    .nCLEAR(nCLEAR), .nLOAD(nLOAD), .Dbe(or_2_out), .X(C), .Dki(sinc_clear_load_2_dki));
  D_Flip_Flop d_ff_1 (
    .clk(CLK), .D(sinc_clear_load_1_dki), .Q(QD), .Qn(d_ff_1_qn), .preset(1'b0), .en(or_3_out), .reset(1'b0));
  and and_7 (and_7_out, QA, d_ff_3_qn, d_ff_1_qn);
  and and_8 (and_8_out, d_ff_1_qn, d_ff_4_qn, QB);
  Sinc_Clear_Load sinc_clear_load_3 (
    .nCLEAR(nCLEAR), .nLOAD(nLOAD), .Dbe(or_4_out), .X(B), .Dki(sinc_clear_load_3_dki));
  D_Flip_Flop d_ff_2 (
    .clk(CLK), .D(sinc_clear_load_2_dki), .Q(QC), .Qn(d_ff_2_qn), .preset(1'b0), .en(or_3_out), .reset(1'b0));
  or or_5 (or_5_out, and_9_out, and_10_out);
  Sinc_Clear_Load sinc_clear_load_4 (
    .nCLEAR(nCLEAR), .nLOAD(nLOAD), .Dbe(or_5_out), .X(A), .Dki(sinc_clear_load_4_dki));
  D_Flip_Flop d_ff_3 (
    .clk(CLK), .D(sinc_clear_load_3_dki), .Q(QB), .Qn(d_ff_3_qn), .preset(1'b0), .en(or_3_out), .reset(1'b0));
  and and_9 (and_9_out, d_ff_1_qn, d_ff_4_qn);
  and and_10 (and_10_out, d_ff_4_qn, d_ff_3_qn);
  D_Flip_Flop d_ff_4 (
    .clk(CLK), .D(sinc_clear_load_4_dki), .Q(QA), .Qn(d_ff_4_qn), .preset(1'b0), .en(or_3_out), .reset(1'b0));
  and and_11 (and_11_out, QD, ~QC, ~QB, QA);  // AND_Gate
  and and_12 (TC, and_11_out, ET);

  // Notes on the sheet:
  //   Decimális számláló szinkron törlő és szinkron beíró bemenettel
endmodule

module _160_Dec_Count_Async_Clear (
  input  nCLEAR,
  input  nLOAD,
  input  D,
  input  C,
  input  B,
  input  A,
  input  ET,
  input  EP,
  input  CLK,
  output TC,
  output QC,
  output QB,
  output QA,
  output QD
);

  wire and_1_out, and_2_out, and_3_out, and_4_out, and_5_out, and_6_out, and_7_out, and_8_out, and_9_out,
       and_10_out, and_11_out, d_ff_1_qn, d_ff_2_qn, d_ff_3_qn, d_ff_4_qn, not_1_out, or_1_out, or_2_out,
       or_3_out, or_4_out, or_5_out, sinc_load_1_dki, sinc_load_2_dki, sinc_load_3_dki, sinc_load_4_dki;

  or or_1 (or_1_out, and_1_out, and_2_out);
  and and_1 (and_1_out, QA, QB, QC);
  and and_2 (and_2_out, d_ff_4_qn, d_ff_2_qn, QD);
  not not_1 (not_1_out, nCLEAR);
  or or_2 (or_2_out, and_4_out, and_5_out, and_6_out);
  and and_3 (and_3_out, ET, EP);
  and and_4 (and_4_out, d_ff_3_qn, QC);
  and and_5 (and_5_out, d_ff_2_qn, QA, QB);
  and and_6 (and_6_out, QB, d_ff_4_qn, QC);
  Sinc_Load sinc_load_1 (.nLOAD(nLOAD), .Dbe(or_1_out), .X(D), .Dki(sinc_load_1_dki));
  or or_3 (or_3_out, ~nLOAD, and_3_out);  // OR_Gate
  or or_4 (or_4_out, and_7_out, and_8_out);
  Sinc_Load sinc_load_2 (.nLOAD(nLOAD), .Dbe(or_2_out), .X(C), .Dki(sinc_load_2_dki));
  D_Flip_Flop d_ff_1 (
    .clk(CLK), .D(sinc_load_1_dki), .Q(QD), .Qn(d_ff_1_qn), .preset(1'b0), .en(or_3_out), .reset(not_1_out));
  and and_7 (and_7_out, QA, d_ff_3_qn, d_ff_1_qn);
  and and_8 (and_8_out, d_ff_1_qn, d_ff_4_qn, QB);
  Sinc_Load sinc_load_3 (.nLOAD(nLOAD), .Dbe(or_4_out), .X(B), .Dki(sinc_load_3_dki));
  D_Flip_Flop d_ff_2 (
    .clk(CLK), .D(sinc_load_2_dki), .Q(QC), .Qn(d_ff_2_qn), .preset(1'b0), .en(or_3_out), .reset(not_1_out));
  or or_5 (or_5_out, and_9_out, and_10_out);
  Sinc_Load sinc_load_4 (.nLOAD(nLOAD), .Dbe(or_5_out), .X(A), .Dki(sinc_load_4_dki));
  D_Flip_Flop d_ff_3 (
    .clk(CLK), .D(sinc_load_3_dki), .Q(QB), .Qn(d_ff_3_qn), .preset(1'b0), .en(or_3_out), .reset(not_1_out));
  and and_9 (and_9_out, d_ff_1_qn, d_ff_4_qn);
  and and_10 (and_10_out, d_ff_4_qn, d_ff_3_qn);
  D_Flip_Flop d_ff_4 (
    .clk(CLK), .D(sinc_load_4_dki), .Q(QA), .Qn(d_ff_4_qn), .preset(1'b0), .en(or_3_out), .reset(not_1_out));
  and and_11 (and_11_out, QD, ~QC, ~QB, QA);  // AND_Gate
  and and_12 (TC, and_11_out, ET);

  // Notes on the sheet:
  //   Decimális számláló aszinkron törlő és szinkron beíró bemenettel
endmodule

module _163_Hex_Sync_Clear (
  input  nCLEAR,
  input  nLOAD,
  input  D,
  input  C,
  input  B,
  input  A,
  input  ET,
  input  EP,
  input  CLK,
  output TC,
  output QD,
  output QC,
  output QB,
  output QA
);

  wire and_1_out, and_2_out, and_3_out, and_4_out, and_5_out, and_6_out, d_ff_4_qn, or_1_out, or_2_out,
       or_3_out, or_4_out, or_5_out, sinc_clear_load_1_dki, sinc_clear_load_2_dki, sinc_clear_load_3_dki,
       sinc_clear_load_4_dki, xor_1_out;

  or or_1 (or_1_out, and_1_out, and_2_out);
  and and_1 (and_1_out, QA, QB, QC, ~QD);  // AND_Gate
  or or_2 (or_2_out, ~QA, ~QB, ~QC);  // OR_Gate
  and and_2 (and_2_out, or_2_out, QD);
  and and_3 (and_3_out, ET, EP);
  Sinc_Clear_Load sinc_clear_load_1 (
    .nCLEAR(nCLEAR), .nLOAD(nLOAD), .Dbe(or_1_out), .X(D), .Dki(sinc_clear_load_1_dki));
  or or_3 (or_3_out, ~nLOAD, and_3_out);  // OR_Gate
  and and_4 (and_4_out, ~QC, QB, QA);  // AND_Gate
  or or_4 (or_4_out, and_4_out, and_5_out);
  and and_5 (and_5_out, or_5_out, QC);
  Sinc_Clear_Load sinc_clear_load_2 (
    .nCLEAR(nCLEAR), .nLOAD(nLOAD), .Dbe(or_4_out), .X(C), .Dki(sinc_clear_load_2_dki));
  D_Flip_Flop d_ff_1 (
    .clk(CLK), .D(sinc_clear_load_1_dki), .Q(QD), .preset(1'b0), .en(or_3_out), .reset(1'b0));  // open: Qn
  or or_5 (or_5_out, ~QA, ~QB);  // OR_Gate
  Sinc_Clear_Load sinc_clear_load_3 (
    .nCLEAR(nCLEAR), .nLOAD(nLOAD), .Dbe(xor_1_out), .X(B), .Dki(sinc_clear_load_3_dki));
  D_Flip_Flop d_ff_2 (
    .clk(CLK), .D(sinc_clear_load_2_dki), .Q(QC), .preset(1'b0), .en(or_3_out), .reset(1'b0));  // open: Qn
  xor xor_1 (xor_1_out, QA, QB);
  Sinc_Clear_Load sinc_clear_load_4 (
    .nCLEAR(nCLEAR), .nLOAD(nLOAD), .Dbe(d_ff_4_qn), .X(A), .Dki(sinc_clear_load_4_dki));
  D_Flip_Flop d_ff_3 (
    .clk(CLK), .D(sinc_clear_load_3_dki), .Q(QB), .preset(1'b0), .en(or_3_out), .reset(1'b0));  // open: Qn
  D_Flip_Flop d_ff_4 (
    .clk(CLK), .D(sinc_clear_load_4_dki), .Q(QA), .Qn(d_ff_4_qn), .preset(1'b0), .en(or_3_out), .reset(1'b0));
  and and_6 (and_6_out, QA, QB, QC, QD);
  and and_7 (TC, and_6_out, ET);

  // Notes on the sheet:
  //   Hexadecimális (bináris) számláló szinkron törlő és szinkron beíró bemenettel
endmodule

module _161_Hex_Count_Async_Clear (
  input  nCLEAR,
  input  nLOAD,
  input  D,
  input  C,
  input  B,
  input  A,
  input  ET,
  input  EP,
  input  CLK,
  output TC,
  output QD,
  output QC,
  output QB,
  output QA
);

  wire and_1_out, and_2_out, and_3_out, and_4_out, and_5_out, and_6_out, d_ff_4_qn, not_1_out, or_1_out,
       or_2_out, or_3_out, or_4_out, or_5_out, sinc_load_1_dki, sinc_load_2_dki, sinc_load_3_dki,
       sinc_load_4_dki, xor_1_out;

  or or_1 (or_1_out, and_1_out, and_2_out);
  not not_1 (not_1_out, nCLEAR);
  and and_1 (and_1_out, QA, QB, QC, ~QD);  // AND_Gate
  or or_2 (or_2_out, ~QA, ~QB, ~QC);  // OR_Gate
  and and_2 (and_2_out, or_2_out, QD);
  and and_3 (and_3_out, ET, EP);
  Sinc_Load sinc_load_1 (.nLOAD(nLOAD), .Dbe(or_1_out), .X(D), .Dki(sinc_load_1_dki));
  or or_3 (or_3_out, ~nLOAD, and_3_out);  // OR_Gate
  and and_4 (and_4_out, ~QC, QB, QA);  // AND_Gate
  or or_4 (or_4_out, and_4_out, and_5_out);
  and and_5 (and_5_out, or_5_out, QC);
  Sinc_Load sinc_load_2 (.nLOAD(nLOAD), .Dbe(or_4_out), .X(C), .Dki(sinc_load_2_dki));
  D_Flip_Flop d_ff_1 (
    .clk(CLK), .D(sinc_load_1_dki), .Q(QD), .preset(1'b0), .en(or_3_out), .reset(not_1_out));  // open: Qn
  or or_5 (or_5_out, ~QA, ~QB);  // OR_Gate
  Sinc_Load sinc_load_3 (.nLOAD(nLOAD), .Dbe(xor_1_out), .X(B), .Dki(sinc_load_3_dki));
  D_Flip_Flop d_ff_2 (
    .clk(CLK), .D(sinc_load_2_dki), .Q(QC), .preset(1'b0), .en(or_3_out), .reset(not_1_out));  // open: Qn
  xor xor_1 (xor_1_out, QA, QB);
  Sinc_Load sinc_load_4 (.nLOAD(nLOAD), .Dbe(d_ff_4_qn), .X(A), .Dki(sinc_load_4_dki));
  D_Flip_Flop d_ff_3 (
    .clk(CLK), .D(sinc_load_3_dki), .Q(QB), .preset(1'b0), .en(or_3_out), .reset(not_1_out));  // open: Qn
  D_Flip_Flop d_ff_4 (
    .clk(CLK), .D(sinc_load_4_dki), .Q(QA), .Qn(d_ff_4_qn), .preset(1'b0), .en(or_3_out), .reset(not_1_out));
  and and_6 (and_6_out, QA, QB, QC, QD);
  and and_7 (TC, and_6_out, ET);

  // Notes on the sheet:
  //   Hexadecimális (bináris) számláló aszinkron törlő és szinkron beíró bemenettel
endmodule
