// Logisim project ellenállás lib.circ as structural Verilog: 2 circuits, main circuit main
module main (
);

  wire \ellenállás_1_out_2 , \ellenállás_2_out_2 ;

  \ellenállás  \ellenállás_1  (.in_1(1'b1), .out_2(\ellenállás_1_out_2 ));
  \ellenállás  \ellenállás_2  (.in_1(1'b0), .out_2(\ellenállás_2_out_2 ));
endmodule

module \ellenállás  (
  input  in_1,
  output out_2
);

  buf buffer_1 (out_2, in_1);
endmodule
