// Logisim project flip flops lib.circ as structural Verilog: 7 circuits, main circuit main
module main (
);

  D_flip_flop d_flip_flop_1 ();  // open: CLK, D, nPR, nCL, Q, nQ
  RS_flip_flop rs_flip_flop_1 ();  // open: S, R, nQ, Q
  T_flip_flop t_flip_flop_1 ();  // open: CLK, T, nPR, nCL, Q, nQ
  nRnS_flip_flop nrns_flip_flop_1 ();  // open: nS, nR, Q, nQ
  JK_flip_flop jk_flip_flop_1 ();  // open: J, CLK, K, nPR, nCL, Q, nQ

  // Notes on the sheet:
  //   D Flip-Flop
  //   RS flip-flop
  //   1 bites tároló elemek - Flip Flop-ok
  //   T Flip-Flop
  //   CLR negált (aszinkron törlő) és PRE negált (aszinkron beíró) bemenet
  //   nR nS Flip-Flop
  //   J-K Flip-Flop
endmodule

module T_flip_flop (
  input  CLK,
  input  T,
  input  nPR,
  input  nCL,
  output Q,
  output nQ
);

  wire not_1_out, not_2_out;

  T_Flip_Flop t_ff_1 (.clk(CLK), .T(T), .Q(Q), .Qn(nQ), .preset(not_1_out), .reset(not_2_out));  // open: en
  not not_1 (not_1_out, nPR);
  not not_2 (not_2_out, nCL);
endmodule

module D_flip_flop (
  input  CLK,
  input  D,
  input  nPR,
  input  nCL,
  output Q,
  output nQ
);

  wire not_1_out, not_2_out;

  D_Flip_Flop d_ff_1 (.clk(CLK), .D(D), .Q(Q), .Qn(nQ), .preset(not_1_out), .reset(not_2_out));  // open: en
  not not_1 (not_1_out, nPR);
  not not_2 (not_2_out, nCL);
endmodule

module JK_flip_flop (
  input  J,
  input  CLK,
  input  K,
  input  nPR,
  input  nCL,
  output Q,
  output nQ
);

  wire not_1_out, not_2_out;

  not not_1 (not_1_out, nPR);
  not not_2 (not_2_out, nCL);
  J_K_Flip_Flop j_k_ff_1 (.J(J), .clk(CLK), .K(K), .Q(Q), .Qn(nQ), .preset(not_1_out), .reset(not_2_out));  // open: en
endmodule

module \JK_negált_flip_flop  (
  input  J,
  input  CLK,
  input  K,
  input  nPR,
  input  nCL,
  output Q,
  output nQ
);

  wire not_1_out, not_2_out, not_3_out;

  not not_1 (not_1_out, K);
  not not_2 (not_2_out, nPR);
  not not_3 (not_3_out, nCL);
  J_K_Flip_Flop j_k_ff_1 (
    .J(J), .clk(CLK), .K(not_1_out), .Q(Q), .Qn(nQ), .preset(not_2_out), .reset(not_3_out));  // open: en
endmodule

module RS_flip_flop (
  input  S,
  input  R,
  output nQ,
  output Q
);

  nor nor_1 (nQ, S, Q);
  nor nor_2 (Q, nQ, R);
endmodule

module nRnS_flip_flop (
  input  nS,
  input  nR,
  output Q,
  output nQ
);

  nand nand_1 (Q, nS, nQ);
  nand nand_2 (nQ, Q, nR);
endmodule
