// Logisim project shift regs lib.circ as structural Verilog: 3 circuits, main circuit main
module main (
);

  HC195_Shift_Reg_Async_Clear hc195_shift_reg_async_clear_1 ();  // open: nCLR, SH_LD, CLK, SI, A, B, C, D, QA, QB, QC, QD, nQD
  Shift_Reg_Sync_Clear shift_reg_sync_clear_1 ();  // open: nCLR, SH_LD, CLK, SI, A, B, C, D, QA, QB, QC, QD, nQD

  // Notes on the sheet:
  //   Léptető regiszter aszinkron törlő és szinkron beíró bemenettel
  //   Léptető regiszter szinkron törlő és szinkron beíró bemenettel
endmodule

module HC195_Shift_Reg_Async_Clear (
  input  nCLR,
  input  SH_LD,
  input  CLK,
  input  SI,
  input  A,
  input  B,
  input  C,
  input  D,
  output QA,
  output QB,
  output QC,
  output QD,
  output nQD
);

  wire not_1_out, sinc_load_1_dki, sinc_load_2_dki, sinc_load_3_dki, sinc_load_4_dki;

  not not_1 (not_1_out, nCLR);
  Sinc_Load sinc_load_1 (.nLOAD(SH_LD), .Dbe(SI), .X(A), .Dki(sinc_load_1_dki));
  D_Flip_Flop d_ff_1 (.clk(CLK), .D(sinc_load_1_dki), .Q(QA), .preset(1'b0), .en(1'b1), .reset(not_1_out));  // open: Qn
  Sinc_Load sinc_load_2 (.nLOAD(SH_LD), .Dbe(QA), .X(B), .Dki(sinc_load_2_dki));
  D_Flip_Flop d_ff_2 (.clk(CLK), .D(sinc_load_2_dki), .Q(QB), .preset(1'b0), .en(1'b1), .reset(not_1_out));  // open: Qn
  Sinc_Load sinc_load_3 (.nLOAD(SH_LD), .Dbe(QB), .X(C), .Dki(sinc_load_3_dki));
  D_Flip_Flop d_ff_3 (.clk(CLK), .D(sinc_load_3_dki), .Q(QC), .preset(1'b0), .en(1'b1), .reset(not_1_out));  // open: Qn
  Sinc_Load sinc_load_4 (.nLOAD(SH_LD), .Dbe(QC), .X(D), .Dki(sinc_load_4_dki));
  D_Flip_Flop d_ff_4 (.clk(CLK), .D(sinc_load_4_dki), .Q(QD), .preset(1'b0), .en(1'b1), .reset(not_1_out));  // open: Qn
  not not_2 (nQD, QD);

  // Notes on the sheet:
  //   Léptető regiszter aszinkron törlő és szinkron beíró bemenettel
endmodule

module Shift_Reg_Sync_Clear (
  input  nCLR,
  input  SH_LD,
  input  CLK,
  input  SI,
  input  A,
  input  B,
  input  C,
  input  D,
  output QA,
  output QB,
  output QC,
  output QD,
  output nQD
);

  wire sinc_clear_load_1_dki, sinc_clear_load_2_dki, sinc_clear_load_3_dki, sinc_clear_load_4_dki;

  Sinc_Clear_Load sinc_clear_load_1 (.nCLEAR(nCLR), .nLOAD(SH_LD), .Dbe(SI), .X(A), .Dki(sinc_clear_load_1_dki));
  D_Flip_Flop d_ff_1 (
    .clk(CLK), .D(sinc_clear_load_1_dki), .Q(QA), .preset(1'b0), .en(1'b1), .reset(1'b0));  // open: Qn
  Sinc_Clear_Load sinc_clear_load_2 (.nCLEAR(nCLR), .nLOAD(SH_LD), .Dbe(QA), .X(B), .Dki(sinc_clear_load_2_dki));
  D_Flip_Flop d_ff_2 (
    .clk(CLK), .D(sinc_clear_load_2_dki), .Q(QB), .preset(1'b0), .en(1'b1), .reset(1'b0));  // open: Qn
  Sinc_Clear_Load sinc_clear_load_3 (.nCLEAR(nCLR), .nLOAD(SH_LD), .Dbe(QB), .X(C), .Dki(sinc_clear_load_3_dki));
  D_Flip_Flop d_ff_3 (
    .clk(CLK), .D(sinc_clear_load_3_dki), .Q(QC), .preset(1'b0), .en(1'b1), .reset(1'b0));  // open: Qn
  Sinc_Clear_Load sinc_clear_load_4 (.nCLEAR(nCLR), .nLOAD(SH_LD), .Dbe(QC), .X(D), .Dki(sinc_clear_load_4_dki));
  D_Flip_Flop d_ff_4 (
    .clk(CLK), .D(sinc_clear_load_4_dki), .Q(QD), .preset(1'b0), .en(1'b1), .reset(1'b0));  // open: Qn
  not not_1 (nQD, QD);

  // Notes on the sheet:
  //   Léptető regiszter szinkron törlő és szinkron beíró bemenettel
endmodule
